// Logisim project su.circ as structural Verilog: 3 circuits, main circuit main
module main (
  input  RUN
);

  wire button_1_out;
  wire [2:0] CPU_CU_t;
  wire [15:0] CPU_PCU_pcout;

  CU CPU_CU (.RUN(RUN), .T(CPU_CU_t));  // open: RstClk, ClkOvr
  PCU CPU_PCU (.RUN(RUN), .RESET(button_1_out), .T(CPU_CU_t), .PCOut(CPU_PCU_pcout));
  Button button_1 (.out(button_1_out));
  ROM #(.dataWidth(32)) PrgmRom (.addr(CPU_PCU_pcout[9:2]));  // open: data

  // Notes on the sheet:
  //   contents of PrgmRom (hex, n*v repeats v):
  //   23 20 73 75 a 54 68 65 20 73 75 20 64 69 67 69 74 61 6c 20 70 72 6f 63 65 73 73 6f 72 a
endmodule

module CU (
  input  RstClk,
  input  RUN,
  output [2:0] T,
  output ClkOvr
);

  wire and_1_out, clock_1_out, State_carry;
  wire [1:0] State_q;

  Clock clock_1 (.out(clock_1_out));
  and and_1 (and_1_out, clock_1_out, RUN);
  Counter #(.max('h2), .width(2)) State (
    .clr(RstClk), .load(1'b0), .up(1'b1), .count(1'b1), .clk(and_1_out), .D(2'b00), .carry(State_carry),
    .Q(State_q));
  // NoConnect on State_carry
  Decoder #(.enable("false"), .select(2)) decoder_1 (
    .out0(T[0]), .out1(T[1]), .out2(T[2]), .out3(ClkOvr), .sel(State_q));
endmodule

module PCU (
  input  RUN,
  input  RESET,
  input  [2:0] T,
  output [15:0] PCOut
);

  wire [15:0] PC_q;

  Register #(.width(16)) PC (.D(PCOut), .en(RUN), .clk(T[2]), .Q(PC_q), .clr(RESET));
  Adder #(.width(16)) adder_1 (.a(PC_q), .b(16'h4), .out(PCOut));  // open: cin, cout
endmodule
